// Logisim project snake1.circ as structural Verilog
module main (
);

  wire and_5_out, BAN, button_1_out, cdm_8_1_data_code_prime, CL, clock_1_out, code, comparator_1_eq,
       comparator_2_eq, data, decoder_2_out0, decoder_2_out1, demultiplexer_2_out0, demultiplexer_2_out1,
       down, globReset, I_Osel, in_out, left, mem, nor_1_out, nor_2_out, not_1_out, not_2_out, not_3_out,
       not_4_out, not_5_out, not_6_out, not_7_out, or_1_out, or_2_out, RAM, right, st, transistor_1_out, up,
       \вторая_часть_адреса_out , \вужик_вогнепальний , \відсік , \Первая_часть_адреса_out ;
  wire [3:0] counter_1_q, counter_2_q;
  wire [6:0] controlled_buffer_1_out, register_1_q;
  wire [7:0] adr, B6_q, cdm_8_1_data_out, cdm_8_1_r0, cdm_8_1_r1, cdm_8_1_r2, cdm_8_1_r3, cdm_8_1_sp,
       controlled_buffer_5_out, dat, demultiplexer_1_out0, demultiplexer_1_out1, eated_q, monitor_1_b0,
       monitor_1_b1, monitor_1_b2, monitor_1_b3, monitor_1_b4, monitor_1_b5, monitor_1_b6, monitor_1_c0,
       monitor_1_c1, monitor_1_c2, monitor_1_c3, monitor_1_c4, monitor_1_c5, monitor_1_c6, monitor_1_c7, pc,
       register_2_q, rom_1_data, rom_2_data, tailVal_q;
  wire [7:4] counter_1_q_2, counter_2_q_2;
  wire [7:7] rs_latch_1_q_prime;
  wire [31:0] displayconnects_1_out_5, displayconnects_1_out_6, displayconnects_1_out_7,
       displayconnects_1_out_8, displayconnects_1_out_9, displayconnects_1_out_10, displayconnects_1_out_11,
       displayconnects_1_out_12, multiplexer_1_out, multiplexer_2_out, multiplexer_3_out, multiplexer_4_out,
       multiplexer_5_out, multiplexer_6_out, multiplexer_7_out, multiplexer_8_out, status_1_out_2,
       status_1_out_3, status_1_out_4, status_1_out_5, status_1_out_6, status_1_out_7, status_1_out_8,
       status_1_out_9, status_1_out_10, status_1_out_11, status_1_out_12, status_1_out_13, status_1_out_14,
       status_1_out_15, status_1_out_16, status_1_out_17, status_1_out_18;

  // Probe on adr
  Clock clock_1 (.out(clock_1_out));
  // Probe on dat
  Demultiplexer #(.width(8), .enable("false")) demultiplexer_1 (
    .out0(demultiplexer_1_out0), .out1(demultiplexer_1_out1), .in(adr), .sel(\відсік ));
  // Probe on cdm_8_1_r0
  or or_1 (or_1_out, button_1_out, globReset);
  and and_1 (CL, ~BAN, clock_1_out);  // AND_Gate
  Button button_1 (.out(button_1_out));
  Transistor #(.\type ("n")) transistor_1 (.in(1'b0), .out(transistor_1_out), .gate(left));
  assign controlled_buffer_1_out = left ? 7'b0000001 : 7'bz;  // Controlled_Buffer controlled_buffer_1
  displayConnects displayconnects_1 (
    .displayReset(globReset), .st(st), .adr(adr), .data(dat), .out_5(displayconnects_1_out_5),
    .out_6(displayconnects_1_out_6), .out_7(displayconnects_1_out_7), .out_8(displayconnects_1_out_8),
    .out_9(displayconnects_1_out_9), .out_10(displayconnects_1_out_10), .out_11(displayconnects_1_out_11),
    .out_12(displayconnects_1_out_12));
  // Probe on cdm_8_1_r2
  // Probe on cdm_8_1_r3
  // Probe on cdm_8_1_r1
  assign controlled_buffer_1_out = right ? {7{1'b0}} : 7'bz;  // Controlled_Buffer controlled_buffer_2
  // Probe on pc
  // Probe on cdm_8_1_sp
  and and_2 (st, data, CL);
  Transistor #(.\type ("n")) transistor_2 (.in(1'b0), .out(transistor_1_out), .gate(right));
  DotMatrix #(.inputtype("row"), .matrixcols(32), .matrixrows(17)) dotmatrix_1 (
    .row0(status_1_out_2), .row1(status_1_out_3), .row2(status_1_out_4), .row3(status_1_out_5),
    .row4(status_1_out_6), .row5(status_1_out_7), .row6(status_1_out_8), .row7(status_1_out_9),
    .row8(status_1_out_10), .row9(status_1_out_11), .row10(status_1_out_12), .row11(status_1_out_13),
    .row12(status_1_out_14), .row13(status_1_out_15), .row14(status_1_out_16), .row15(status_1_out_17),
    .row16(status_1_out_18));
  status status_1 (
    .ban(not_1_out), .out_2(status_1_out_2), .out_3(status_1_out_3), .out_4(status_1_out_4),
    .out_5(status_1_out_5), .out_6(status_1_out_6), .out_7(status_1_out_7), .out_8(status_1_out_8),
    .out_9(status_1_out_9), .out_10(status_1_out_10), .out_11(status_1_out_11), .out_12(status_1_out_12),
    .out_13(status_1_out_13), .out_14(status_1_out_14), .out_15(status_1_out_15), .out_16(status_1_out_16),
    .out_17(status_1_out_17), .out_18(status_1_out_18));
  not not_1 (not_1_out, BAN);
  DotMatrix #(.inputtype("row"), .matrixcols(32), .matrixrows(32)) dotmatrix_2 (
    .row0(multiplexer_1_out), .row1(multiplexer_1_out), .row2(multiplexer_1_out), .row3(multiplexer_1_out),
    .row4(multiplexer_2_out), .row5(multiplexer_2_out), .row6(multiplexer_2_out), .row7(multiplexer_2_out),
    .row8(multiplexer_3_out), .row9(multiplexer_3_out), .row10(multiplexer_3_out), .row11(multiplexer_3_out),
    .row12(multiplexer_4_out), .row13(multiplexer_4_out), .row14(multiplexer_4_out),
    .row15(multiplexer_4_out), .row16(multiplexer_5_out), .row17(multiplexer_5_out),
    .row18(multiplexer_5_out), .row19(multiplexer_5_out), .row20(multiplexer_6_out),
    .row21(multiplexer_6_out), .row22(multiplexer_6_out), .row23(multiplexer_6_out),
    .row24(multiplexer_7_out), .row25(multiplexer_7_out), .row26(multiplexer_7_out),
    .row27(multiplexer_7_out), .row28(multiplexer_8_out), .row29(multiplexer_8_out),
    .row30(multiplexer_8_out), .row31(multiplexer_8_out));
  Multiplexer #(.width(32), .enable("false")) multiplexer_1 (
    .in0(displayconnects_1_out_5), .out(multiplexer_1_out), .sel(BAN));  // open: in1
  Multiplexer #(.width(32), .enable("false")) multiplexer_2 (
    .in0(displayconnects_1_out_6), .out(multiplexer_2_out), .sel(BAN));  // open: in1
  Multiplexer #(.width(32), .enable("false")) multiplexer_3 (
    .in0(displayconnects_1_out_7), .out(multiplexer_3_out), .sel(BAN));  // open: in1
  Multiplexer #(.width(32), .enable("false")) multiplexer_4 (
    .in0(displayconnects_1_out_8), .out(multiplexer_4_out), .sel(BAN));  // open: in1
  Multiplexer #(.width(32), .enable("false")) multiplexer_5 (
    .in0(displayconnects_1_out_9), .out(multiplexer_5_out), .sel(BAN));  // open: in1
  Multiplexer #(.width(32), .enable("false")) multiplexer_6 (
    .in0(displayconnects_1_out_10), .out(multiplexer_6_out), .sel(BAN));  // open: in1
  Multiplexer #(.width(32), .enable("false")) multiplexer_7 (
    .in0(displayconnects_1_out_11), .out(multiplexer_7_out), .sel(BAN));  // open: in1
  Multiplexer #(.width(32), .enable("false")) multiplexer_8 (
    .in0(displayconnects_1_out_12), .out(multiplexer_8_out), .sel(BAN));  // open: in1
  LED led_1 (.in(BAN));
  CdM_8 cdm_8_1 (
    .data_code_prime(cdm_8_1_data_code_prime), .R0(cdm_8_1_r0), .R1(cdm_8_1_r1), .mem(mem), .R2(cdm_8_1_r2),
    .load_st_prime(in_out), .R3(cdm_8_1_r3), .addr(adr), .PC(pc), .SP(cdm_8_1_sp),
    .data_out(cdm_8_1_data_out), .data_in(controlled_buffer_5_out), .clk(CL), .rset(or_1_out));  // open: page, PS, IAck, IRQ, vector, shadow
  Transistor #(.\type ("n")) transistor_3 (.in(1'b0), .out(transistor_1_out), .gate(up));
  assign controlled_buffer_1_out = up ? 7'b0000010 : 7'bz;  // Controlled_Buffer controlled_buffer_3
  nor nor_1 (nor_1_out, transistor_1_out, not_2_out);
  not not_2 (not_2_out, transistor_1_out);
  nor nor_2 (nor_2_out, decoder_2_out1, not_3_out);
  not not_3 (not_3_out, decoder_2_out1);
  Decoder #(.disabled(0)) decoder_1 (.out0(code), .out1(data), .sel(cdm_8_1_data_code_prime), .en(mem));
  assign dat = not_4_out ? cdm_8_1_data_out : 8'bz;  // Controlled_Buffer controlled_buffer_4
  not not_4 (not_4_out, in_out);
  assign controlled_buffer_5_out = in_out ? dat : 8'bz;  // Controlled_Buffer controlled_buffer_5
  Transistor #(.\type ("n")) transistor_4 (.in(1'b0), .out(transistor_1_out), .gate(down));
  assign controlled_buffer_1_out = down ? 7'b0000011 : 7'bz;  // Controlled_Buffer controlled_buffer_6
  Button Restart (.out(globReset));
  Button button_2 (.out(left));
  // Probe on adr
  not not_5 (not_5_out, transistor_1_out);
  Pull_Resistor #(.pull(1)) pull_resistor_1 (.node(transistor_1_out));
  Register #(.width(7), .trigger("high")) register_1 (
    .D(controlled_buffer_1_out), .Q(register_1_q), .clk(not_6_out));  // open: en, clr
  Button button_3 (.out(up));
  Button button_4 (.out(right));
  Button button_5 (.out(down));
  not not_6 (not_6_out, not_5_out);
  RS_latch rs_latch_1 (.S(nor_1_out), .R(nor_2_out), .Q_prime(rs_latch_1_q_prime[7]));  // open: Q, reset
  ROM rom_1 (.addr(demultiplexer_1_out1), .data(rom_1_data), .sel(demultiplexer_2_out1));
  ROM rom_2 (.addr(demultiplexer_1_out0), .data(rom_2_data), .sel(demultiplexer_2_out0));
  RAM ram_1 (.addr(adr), .data(dat), .sel(RAM), .clk(CL), .ld(in_out), .clr(globReset));
  assign dat = decoder_2_out1 ? {rs_latch_1_q_prime[7], register_1_q} : 8'bz;  // Controlled_Buffer controlled_buffer_7
  Multiplexer #(.width(8), .enable("false")) multiplexer_9 (
    .in0(rom_2_data), .in1(rom_1_data), .out(dat), .sel(\відсік ));
  Hex_Digit_Display hex_digit_display_1 (.value(counter_2_q));  // open: dp
  Demultiplexer #(.enable("false")) demultiplexer_2 (
    .out0(demultiplexer_2_out0), .out1(demultiplexer_2_out1), .in(code), .sel(\відсік ));
  Hex_Digit_Display hex_digit_display_2 (.value(register_2_q[7:4]));  // open: dp
  Register register_2 (.D(dat), .Q(register_2_q), .clk(decoder_2_out0));  // open: en, clr
  Hex_Digit_Display hex_digit_display_3 (.value(counter_1_q));  // open: dp
  Register C0 (.D(monitor_1_c0), .clk(st));  // open: en, Q, clr
  and \u_вторая_часть_адреса  (\вторая_часть_адреса_out , I_Osel, adr[0], adr[1], ~adr[2], ~adr[3]);  // AND_Gate
  Hex_Digit_Display hex_digit_display_4 (.value(register_2_q[3:0]));  // open: dp
  Register adr_of_storing_Head__C0_CX (.D(monitor_1_b0), .clk(st));  // open: en, Q, clr
  Register C1 (.D(monitor_1_c1), .clk(st));  // open: en, Q, clr
  Register C2 (.D(monitor_1_c2), .clk(st));  // open: en, Q, clr
  Decoder #(.disabled(0)) decoder_2 (
    .out0(decoder_2_out0), .out1(decoder_2_out1), .sel(in_out), .en(\вторая_часть_адреса_out ));
  Register adr_of_storing_Tail (.D(monitor_1_b1), .clk(st));  // open: en, Q, clr
  Register C3 (.D(monitor_1_c3), .clk(st));  // open: en, Q, clr
  and and_3 (I_Osel, not_7_out, CL, data);
  Register C4 (.D(monitor_1_c4), .clk(st));  // open: en, Q, clr
  Register C5 (.D(monitor_1_c5), .clk(st));  // open: en, Q, clr
  not not_7 (not_7_out, \Первая_часть_адреса_out );
  Comparator comparator_1 (.a({8{1'b0}}), .b(eated_q), .eq(comparator_1_eq));  // open: gt, lt
  Register C7 (.D(monitor_1_c7), .clk(st));  // open: en, Q, clr
  Register C6 (.D(monitor_1_c6), .clk(st));  // open: en, Q, clr
  nand \u_Первая_часть_адреса  (\Первая_часть_адреса_out , ~adr[4], adr[5], adr[6], adr[7]);  // NAND_Gate
  and and_4 (RAM, \Первая_часть_адреса_out , data);
  Counter #(.max('ha)) counter_1 (
    .Q({counter_1_q_2, counter_1_q}), .clk(comparator_1_eq), .clr(or_2_out));  // open: load, D, count, carry
  Register tailVal (.D(monitor_1_b2), .Q(tailVal_q), .clk(st));  // open: en, clr
  Register B6 (.D(monitor_1_b6), .Q(B6_q), .clk(st), .clr(globReset));  // open: en
  \раздатчик_банов  \u_раздатчик_банов_1  (.B6(B6_q), .reset(globReset), .BAN(BAN));
  Comparator comparator_2 (.a(8'ha), .b({counter_1_q_2, counter_1_q}), .eq(comparator_2_eq));  // open: gt, lt
  // Probe on tailVal_q
  Register tailStr (.D(monitor_1_b3), .clk(st));  // open: en, Q, clr
  Counter counter_2 (
    .Q({counter_2_q_2, counter_2_q}), .clk(and_5_out), .clr(globReset));  // open: load, D, count, carry
  and and_5 (and_5_out, comparator_2_eq, comparator_1_eq);
  or or_2 (or_2_out, and_5_out, globReset);
  Register eated (.D(monitor_1_b4), .Q(eated_q), .clk(st));  // open: en, clr
  monitor monitor_1 (
    .B5(monitor_1_b5), .B4(monitor_1_b4), .B3(monitor_1_b3), .B2(monitor_1_b2), .B1(monitor_1_b1),
    .B0(monitor_1_b0), .B6(monitor_1_b6), .C7(monitor_1_c7), .C6(monitor_1_c6), .C5(monitor_1_c5),
    .C4(monitor_1_c4), .C3(monitor_1_c3), .C2(monitor_1_c2), .C1(monitor_1_c1), .C0(monitor_1_c0), .adr(adr),
    .dat(dat));
  Register buffer_chain (.D(monitor_1_b5), .clk(st));  // open: en, Q, clr
  Pull_Resistor pull_resistor_2 (.node(adr[0]));
  Pull_Resistor pull_resistor_3 (.node(adr[1]));
  Pull_Resistor pull_resistor_4 (.node(adr[2]));
  Pull_Resistor pull_resistor_5 (.node(adr[3]));
  Pull_Resistor pull_resistor_6 (.node(adr[4]));
  Pull_Resistor pull_resistor_7 (.node(adr[5]));
  Pull_Resistor pull_resistor_8 (.node(adr[6]));
  Pull_Resistor pull_resistor_9 (.node(adr[7]));
  Comparator comparator_3 (.a(pc), .b(8'hf8), .eq(\вужик_вогнепальний ));  // open: gt, lt
  T_Flip_Flop t_ff_1 (.clk(\вужик_вогнепальний ), .T(1'b1), .Q(\відсік ));  // open: Qn, preset, reset, en

  // Other names for the same wires on the sheet: I_Oadr[3:0] = adr[3:0]; I_Odat[7:0] = dat; rd_wr = in_out

  // Notes on the sheet:
  //   contents of rom_1 (hex, n*v repeats v):
  //   d0 a0 b1 5 e1 21 d1 b3 b5 d2 b2 ba 4*9e b7 c 5b 6c 0 e0 1f a7 d0 a0 a1 8c a2 8c a1 ee 21 ee f8 213*0
  //   ee
  //   contents of rom_2 (hex, n*v repeats v):
  //   d0 b0 d1 80 a1 8c d1 82 a1 8c d1 10 a1 8c d1 d0 a1 8c a1 8c d1 97 a1 d2 4 d3 d0 d0 e3 35 c1 c4 d0 e3
  //   c1 c5 5 e1 2c 92 d6 c7 ee 43 d0 1 74 e1 36 96 d6 c7 ee 43 d0 2 74 e1 40 8b d6 c7 ee 43 8f d6 c7 d0
  //   e3 c3 c0 c2 c1 d0 f 43 d0 7 7c e9 53 d6 f1 d1 b4 b5 5 e0 8e d2 b2 ba d3 b3 bf d1 b1 b5 b5 5 e1 6e d6
  //   eb d0 b2 92 a2 ee 8e d0 1 74 e1 7b d6 eb d0 b2 96 a2 ee 8e d0 2 74 e1 88 d6 eb d0 b3 8b a3 ee 8e d6
  //   eb d0 b3 8f a3 d1 b0 b5 c4 a4 c0 d2 b0 d6 bc 8e d1 b4 b5 5 e0 a4 b9 d6 bc ee ab d0 a0 35 a1 d1 b4 a5
  //   ee f8 c5 c6 c4 c7 c1 b1 5 e4 23 a1 c4 4 c0 ee 1f 89 d3 80 7d e9 c5 d0 b5 b1 a9 d7 c0 c1 c2 bc 1 58
  //   ac 61 d0 b4 a1 5 e1 e7 d0 a1 d1 a2 b0 b5 72 e1 e5 77 e0 e3 d6 f1 ee e7 d6 f1 c6 c5 c4 d7 bc 82 48 ac
  //   82 d7 d0 b6 d1 ff a1 d7 0 ee ad
  //   00 right
  //   01 left
  //   10 up
  //   11 down
endmodule

module \розширювачі  (
  input  [7:0] in,
  output [31:0] Out
);


  assign Out = {{4{in[7]}}, {4{in[6]}}, {4{in[5]}}, {4{in[4]}}, {4{in[3]}}, {4{in[2]}}, {4{in[1]}}, {4{in[0]}}};
endmodule

module displayConnects (
  input  displayReset,
  input  st,
  input  [7:0] adr,
  input  [7:0] data,
  output [31:0] out_5,
  output [31:0] out_6,
  output [31:0] out_7,
  output [31:0] out_8,
  output [31:0] out_9,
  output [31:0] out_10,
  output [31:0] out_11,
  output [31:0] out_12
);

  wire d0_2_out, d1_2_out, d2_2_out, d3_2_out, d4_2_out, d5_2_out, d6_2_out, d7_2_out;
  wire [7:0] controlled_buffer_1_out, controlled_buffer_2_out, controlled_buffer_3_out,
       controlled_buffer_4_out, controlled_buffer_5_out, controlled_buffer_6_out, controlled_buffer_7_out,
       controlled_buffer_8_out, D0_q, D1_q, D2_q, D3_q, D4_q, D5_q, D6_q, D7_q;

  Register D0 (.D(controlled_buffer_1_out), .Q(D0_q), .clk(st), .clr(displayReset));  // open: en
  Register D1 (.D(controlled_buffer_2_out), .Q(D1_q), .clk(st), .clr(displayReset));  // open: en
  Register D2 (.D(controlled_buffer_3_out), .Q(D2_q), .clk(st), .clr(displayReset));  // open: en
  Register D3 (.D(controlled_buffer_4_out), .Q(D3_q), .clk(st), .clr(displayReset));  // open: en
  Register D4 (.D(controlled_buffer_5_out), .Q(D4_q), .clk(st), .clr(displayReset));  // open: en
  Register D5 (.D(controlled_buffer_6_out), .Q(D5_q), .clk(st), .clr(displayReset));  // open: en
  Register D6 (.D(controlled_buffer_7_out), .Q(D6_q), .clk(st), .clr(displayReset));  // open: en
  Register D7 (.D(controlled_buffer_8_out), .Q(D7_q), .clk(st), .clr(displayReset));  // open: en
  \розширювачі  \u_розширювачі_1  (.in(D0_q), .Out(out_5));
  \розширювачі  \u_розширювачі_2  (.in(D1_q), .Out(out_6));
  \розширювачі  \u_розширювачі_3  (.in(D2_q), .Out(out_7));
  \розширювачі  \u_розширювачі_4  (.in(D3_q), .Out(out_8));
  \розширювачі  \u_розширювачі_5  (.in(D4_q), .Out(out_9));
  \розширювачі  \u_розширювачі_6  (.in(D5_q), .Out(out_10));
  \розширювачі  \u_розширювачі_7  (.in(D6_q), .Out(out_11));
  \розширювачі  \u_розширювачі_8  (.in(D7_q), .Out(out_12));
  assign controlled_buffer_1_out = d0_2_out ? data : 8'bz;  // Controlled_Buffer controlled_buffer_1
  and d0_2 (d0_2_out, adr[7], adr[6], ~adr[5], adr[4], ~adr[3], ~adr[2], ~adr[1], ~adr[0]);  // AND_Gate
  assign controlled_buffer_2_out = d1_2_out ? data : 8'bz;  // Controlled_Buffer controlled_buffer_2
  and d1_2 (d1_2_out, adr[7], adr[6], ~adr[5], adr[4], ~adr[3], ~adr[2], ~adr[1], adr[0]);  // AND_Gate
  assign controlled_buffer_3_out = d2_2_out ? data : 8'bz;  // Controlled_Buffer controlled_buffer_3
  and d2_2 (d2_2_out, adr[7], adr[6], ~adr[5], adr[4], ~adr[3], ~adr[2], adr[1], ~adr[0]);  // AND_Gate
  assign controlled_buffer_4_out = d3_2_out ? data : 8'bz;  // Controlled_Buffer controlled_buffer_4
  and d3_2 (d3_2_out, adr[7], adr[6], ~adr[5], adr[4], ~adr[3], ~adr[2], adr[1], adr[0]);  // AND_Gate
  assign controlled_buffer_5_out = d4_2_out ? data : 8'bz;  // Controlled_Buffer controlled_buffer_5
  and d4_2 (d4_2_out, adr[7], adr[6], ~adr[5], adr[4], ~adr[3], adr[2], ~adr[1], ~adr[0]);  // AND_Gate
  assign controlled_buffer_6_out = d5_2_out ? data : 8'bz;  // Controlled_Buffer controlled_buffer_6
  and d5_2 (d5_2_out, adr[7], adr[6], ~adr[5], adr[4], ~adr[3], adr[2], ~adr[1], adr[0]);  // AND_Gate
  assign controlled_buffer_7_out = d6_2_out ? data : 8'bz;  // Controlled_Buffer controlled_buffer_7
  and d6_2 (d6_2_out, adr[7], adr[6], ~adr[5], adr[4], ~adr[3], adr[2], adr[1], ~adr[0]);  // AND_Gate
  assign controlled_buffer_8_out = d7_2_out ? data : 8'bz;  // Controlled_Buffer controlled_buffer_8
  and d7_2 (d7_2_out, adr[7], adr[6], ~adr[5], adr[4], ~adr[3], adr[2], adr[1], adr[0]);  // AND_Gate

  // Other names for the same wires on the sheet: stepahka = st
endmodule

module monitor (
  input  [7:0] adr,
  input  [7:0] dat,
  output [7:0] B5,
  output [7:0] B4,
  output [7:0] B3,
  output [7:0] B2,
  output [7:0] B1,
  output [7:0] B0,
  output [7:0] B6,
  output [7:0] C7,
  output [7:0] C6,
  output [7:0] C5,
  output [7:0] C4,
  output [7:0] C3,
  output [7:0] C2,
  output [7:0] C1,
  output [7:0] C0
);

  wire b0_out, b1_out, b2_out, b3_out, b4_out, b5_out, B6_out, c0_out, c1_out, c2_out, c3_out, c4_out,
       c5_out, c6_out, c7_out;

  assign B6 = B6_out ? dat : 8'bz;  // Controlled_Buffer controlled_buffer_1
  and u_B6 (B6_out, adr[7], ~adr[6], adr[5], adr[4], ~adr[3], adr[2], adr[1], ~adr[0]);  // AND_Gate
  assign C0 = c0_out ? dat : 8'bz;  // Controlled_Buffer controlled_buffer_2
  and u_c0 (c0_out, adr[7], adr[6], ~adr[5], ~adr[4], ~adr[3], ~adr[2], ~adr[1], ~adr[0]);  // AND_Gate
  assign C1 = c1_out ? dat : 8'bz;  // Controlled_Buffer controlled_buffer_3
  and u_c1 (c1_out, adr[7], adr[6], ~adr[5], ~adr[4], ~adr[3], ~adr[2], ~adr[1], adr[0]);  // AND_Gate
  assign C2 = c2_out ? dat : 8'bz;  // Controlled_Buffer controlled_buffer_4
  and u_c2 (c2_out, adr[7], adr[6], ~adr[5], ~adr[4], ~adr[3], ~adr[2], adr[1], ~adr[0]);  // AND_Gate
  assign C3 = c3_out ? dat : 8'bz;  // Controlled_Buffer controlled_buffer_5
  and u_c3 (c3_out, adr[7], adr[6], ~adr[5], ~adr[4], ~adr[3], ~adr[2], adr[1], adr[0]);  // AND_Gate
  assign C4 = c4_out ? dat : 8'bz;  // Controlled_Buffer controlled_buffer_6
  and u_c4 (c4_out, adr[7], adr[6], ~adr[5], ~adr[4], ~adr[3], adr[2], ~adr[1], ~adr[0]);  // AND_Gate
  assign C5 = c5_out ? dat : 8'bz;  // Controlled_Buffer controlled_buffer_7
  and u_c5 (c5_out, adr[7], adr[6], ~adr[5], ~adr[4], ~adr[3], adr[2], ~adr[1], adr[0]);  // AND_Gate
  assign C6 = c6_out ? dat : 8'bz;  // Controlled_Buffer controlled_buffer_8
  assign B0 = b0_out ? dat : 8'bz;  // Controlled_Buffer controlled_buffer_9
  and u_b0 (b0_out, adr[7], ~adr[6], adr[5], adr[4], ~adr[3], ~adr[2], ~adr[1], ~adr[0]);  // AND_Gate
  and u_c6 (c6_out, adr[7], adr[6], ~adr[5], ~adr[4], ~adr[3], adr[2], adr[1], ~adr[0]);  // AND_Gate
  assign B1 = b1_out ? dat : 8'bz;  // Controlled_Buffer controlled_buffer_10
  assign C7 = c7_out ? dat : 8'bz;  // Controlled_Buffer controlled_buffer_11
  and u_c7 (c7_out, adr[7], adr[6], ~adr[5], ~adr[4], ~adr[3], adr[2], adr[1], adr[0]);  // AND_Gate
  and u_b1 (b1_out, adr[7], ~adr[6], adr[5], adr[4], ~adr[3], ~adr[2], ~adr[1], adr[0]);  // AND_Gate
  assign B2 = b2_out ? dat : 8'bz;  // Controlled_Buffer controlled_buffer_12
  and u_b2 (b2_out, adr[7], ~adr[6], adr[5], adr[4], ~adr[3], ~adr[2], adr[1], ~adr[0]);  // AND_Gate
  assign B3 = b3_out ? dat : 8'bz;  // Controlled_Buffer controlled_buffer_13
  and u_b3 (b3_out, adr[7], ~adr[6], adr[5], adr[4], ~adr[3], ~adr[2], adr[1], adr[0]);  // AND_Gate
  assign B4 = b4_out ? dat : 8'bz;  // Controlled_Buffer controlled_buffer_14
  and u_b4 (b4_out, adr[7], ~adr[6], adr[5], adr[4], ~adr[3], adr[2], ~adr[1], ~adr[0]);  // AND_Gate
  assign B5 = b5_out ? dat : 8'bz;  // Controlled_Buffer controlled_buffer_15
  and u_b5 (b5_out, adr[7], ~adr[6], adr[5], adr[4], ~adr[3], adr[2], ~adr[1], adr[0]);  // AND_Gate

  // Notes on the sheet:
  //   B6: pull=down
endmodule

module \стриманiсть  (
  input  in_1,
  output out_2
);

  wire counter_1_q;

  Counter #(.width(1), .max('h1)) counter_1 (.count(in_1), .Q(counter_1_q));  // open: load, D, carry, clk, clr
  Comparator comparator_1 ();  // open: a, b, gt, eq, lt
endmodule

module \раздатчик_банов  (
  input  [7:0] B6,
  input  reset,
  output BAN
);

  wire and_1_out;

  and and_1 (and_1_out, B6[0], B6[1], B6[2], B6[3], B6[4], B6[5], B6[6], B6[7]);
  T_Flip_Flop t_ff_1 (.T(1'b1), .Q(BAN), .preset(and_1_out), .reset(reset));  // open: clk, Qn, en
endmodule

module \рахунок  (
  input  [7:0] in_1,
  input  [7:0] in_2,
  output [7:0] out_3
);

  wire comparator_1_lt;
  wire [7:0] subtractor_1_out, subtractor_2_out;

  Comparator comparator_1 (.a(in_1), .b(in_2), .lt(comparator_1_lt));  // open: gt, eq
  Subtractor subtractor_1 (.a(in_1), .b(in_2), .out(subtractor_1_out));  // open: bin, bout
  Subtractor subtractor_2 (.a(in_2), .b(in_1), .out(subtractor_2_out));  // open: bin, bout
  Multiplexer #(.width(8), .enable("false")) multiplexer_1 (
    .in0(subtractor_1_out), .in1(subtractor_2_out), .out(out_3), .sel(comparator_1_lt));
endmodule

module status (
  input  ban,
  output [31:0] out_2,
  output [31:0] out_3,
  output [31:0] out_4,
  output [31:0] out_5,
  output [31:0] out_6,
  output [31:0] out_7,
  output [31:0] out_8,
  output [31:0] out_9,
  output [31:0] out_10,
  output [31:0] out_11,
  output [31:0] out_12,
  output [31:0] out_13,
  output [31:0] out_14,
  output [31:0] out_15,
  output [31:0] out_16,
  output [31:0] out_17,
  output [31:0] out_18
);

  Multiplexer #(.width(32), .enable("false")) multiplexer_1 (
    .in0({32{1'b0}}), .in1({32{1'b0}}), .out(out_2), .sel(ban));
  Multiplexer #(.width(32), .enable("false")) multiplexer_2 (
    .in0(32'h7f7f417e), .in1({32{1'b0}}), .out(out_3), .sel(ban));
  Multiplexer #(.width(32), .enable("false")) multiplexer_3 (
    .in0(32'h40416340), .in1({32{1'b0}}), .out(out_4), .sel(ban));
  Multiplexer #(.width(32), .enable("false")) multiplexer_4 (
    .in0(32'h40417740), .in1({32{1'b0}}), .out(out_5), .sel(ban));
  Multiplexer #(.width(32), .enable("false")) multiplexer_5 (
    .in0(32'h5f7f5d7e), .in1({32{1'b0}}), .out(out_6), .sel(ban));
  Multiplexer #(.width(32), .enable("false")) multiplexer_6 (
    .in0(32'h41414140), .in1({32{1'b0}}), .out(out_7), .sel(ban));
  Multiplexer #(.width(32), .enable("false")) multiplexer_7 (
    .in0(32'h41414140), .in1({32{1'b0}}), .out(out_8), .sel(ban));
  Multiplexer #(.width(32), .enable("false")) multiplexer_8 (
    .in0(32'h7f41417e), .in1({32{1'b0}}), .out(out_9), .sel(ban));
  Multiplexer #(.width(32), .enable("false")) multiplexer_9 (
    .in0({32{1'b0}}), .in1({32{1'b0}}), .out(out_10), .sel(ban));
  Multiplexer #(.width(32), .enable("false")) multiplexer_10 (
    .in0(32'h7f417efe), .in1({32{1'b0}}), .out(out_11), .sel(ban));
  Multiplexer #(.width(32), .enable("false")) multiplexer_11 (
    .in0(32'h41634082), .in1({32{1'b0}}), .out(out_12), .sel(ban));
  Multiplexer #(.width(32), .enable("false")) multiplexer_12 (
    .in0(32'h41224082), .in1({32{1'b0}}), .out(out_13), .sel(ban));
  Multiplexer #(.width(32), .enable("false")) multiplexer_13 (
    .in0(32'h41367efe), .in1({32{1'b0}}), .out(out_14), .sel(ban));
  Multiplexer #(.width(32), .enable("false")) multiplexer_14 (
    .in0(32'h41144098), .in1({32{1'b0}}), .out(out_15), .sel(ban));
  Multiplexer #(.width(32), .enable("false")) multiplexer_15 (
    .in0(32'h411c408c), .in1({32{1'b0}}), .out(out_16), .sel(ban));
  Multiplexer #(.width(32), .enable("false")) multiplexer_16 (
    .in0(32'h7f087e86), .in1({32{1'b0}}), .out(out_17), .sel(ban));
  Multiplexer #(.width(32), .enable("false")) multiplexer_17 (
    .in0({32{1'b0}}), .in1({32{1'b0}}), .out(out_18), .sel(ban));
endmodule
